# Fritzing sketch rfm69_TEENSY_servo (saved by Fritzing 0.9.6b)
breadboards: 1

parts:
  Part2 = Adafruit RFM69HCW Transceiver Radio [part_number="Adafruit #3070 and #3071"]
  Teensy1 = Teensy 4.1
  J1 = Basic Servo

nets:
  VIN: Part2.VIN, Teensy1.3V3_LOW, J1.vcc
  GND: Part2.GND, Teensy1.GND2#31, J1.gnd
  N1: Part2.DIO0, Teensy1.D2
  N2: Part2.SCK, Teensy1.D13
  N3: Part2.MISO, Teensy1.D12
  N4: Part2.MOSI, Teensy1.D11
  N5: Part2.CS, Teensy1.D10
  N6: Part2.RST, Teensy1.D3
  N7: Teensy1.GND, Teensy1.GND2#55
  N8: Teensy1.D9, J1.pulse

notes:
  Teensy is 3V logic level, connect radio power to 3V pin!
  Connect radio to SPI pins and as described in code

custom parts:
  Adafruit RFM69HCW Transceiver Radio: Sending data over long distances is like magic, and now you can be a magician with this range of powerful and easy-to-use radio modules. Sure, sometimes you want to talk to a computer (a good time to use WiFi) or perhaps communicate with a Phone (choose Bluetooth Low Energy!) but what if you want to send data very far? Most WiFi, Bluetooth, Zigbee and other wireless chipsets use 2.4GHz, which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
  Teensy 4.1: The Teensy is a complete USB-based microcontoller development system, in a very small footprint, capable of implementing many types of projects. All programming is done via the USB port. No special programmer is needed, only a standard micro-USB cable and a PC or Macintosh with a USB port.
